# Fritzing sketch 3_in_1_robot (saved by Fritzing 0.9.9b)
circuit board: 10.255cm x 13.0675cm
breadboards: 1

parts:
  Left-Front = gear-motor
  Right-Front = gear-motor
  Right-Back = gear-motor
  Arduino_Nano = Arduino Nano (Rev3.0)
  HC-SR04 = HC-SR04 Ultrasonic Distance Sensor
  IR-receiver = KY-022 Infrared Receiver Module [package="Breakout board"]
  DGServo_9g = Dagu DGServo 9g (Top view) [part_number=RS001B]
  L298N = L298N DC motor driver
  Left-Back = gear-motor
  VCC1 = Battery
  Part1 = Bluetooth HC-06 Macho

nets:
  N1: Left-Front.pin_1, L298N.OUT4, Left-Back.pin_2
  N2: Left-Front.pin_2, L298N.OUT3, Left-Back.pin_1
  N3: Right-Front.pin_1, Right-Back.pin_2, L298N.OUT1
  N4: Right-Front.pin_2, Right-Back.pin_1, L298N.OUT2
  N5: Arduino_Nano.D1/TX, Part1.RXD
  N6: Arduino_Nano.D0/RX, Part1.TXD
  GND: Arduino_Nano.GND, HC-SR04.GND, IR-receiver.-, DGServo_9g.gnd, L298N.GND, VCC1.-, Part1.GND
  N7: Arduino_Nano.D2, HC-SR04.ECHO
  N8: Arduino_Nano.D3, HC-SR04.TRIG
  N9: Arduino_Nano.D4, L298N.IN4
  N10: Arduino_Nano.D5, L298N.IN3
  N11: Arduino_Nano.D6, L298N.IN2
  N12: Arduino_Nano.D7, L298N.IN1
  N13: Arduino_Nano.D8, IR-receiver.S
  N14: Arduino_Nano.D9, DGServo_9g.pulse
  VIN: Arduino_Nano.VIN, L298N.12V, VCC1.+
  VCC: Arduino_Nano.5V, HC-SR04.VCC, IR-receiver.Vin, DGServo_9g.vcc, Part1.VCC

custom parts:
  KY-022 Infrared Receiver Module: KY-022 IR receiver module, reacts to 38kHz infrared light.
  L298N DC motor driver: 2x DC motor driver with 78M05 positive voltage regulator (7..35 V) L298N: max 46 V, 2 A Set 5 V Enable jumper to enable 5 V regultor (needed for the L298N) and +5 V output at screw terminal or supply external +5 V at screw terminal Set ENA and/or ENB to +5 V to enable motor permanently or supply ENA and/or ENB with PWM signal IN1 and IN2 set rotation directory for motor A (OUT1/OUT2) IN2 and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
  Battery: Your standard 2x 18650 battery pack (7.4 Volts)
